# Fritzing sketch dirtbomb_1.1 (saved by Fritzing 0.9.3b)

parts:
  Componente1 = Arduino Uno (Rev3)
  LCD1 = LCD screen
  BAT1 = BC9VPC [package=bc9vpc]  # not connected
  U1 = POT [package=pot_alpha_rv16af-20]  # not connected
  J1 = Piezo Speaker  # not connected
  LED1 = RGB LED (com. cathode, rgb) [package="5 mm [THT]"]
  J2 = female pin header, 2 pins [form="♀ (female)"]
  J3 = female pin header, 2 pins [form="♀ (female)"]
  J4 = female pin header, 2 pins [form="♀ (female)"]
  J5 = female pin header, 2 pins [form="♀ (female)"]
  F1 = FUSE [package=fuse_5mm]
  S1 = Momentary Switch [package=ksa_sealed_tac_switch]
  S2 = Momentary Switch [package=ksa_sealed_tac_switch]
  Mosfet = screw terminal, 3 pins

nets:
  N1: Componente1.A0, J4.pin1
  N2: Componente1.A1, J4.pin2
  N3: Componente1.A2, J2.pin1, S1.4
  N4: Componente1.A3, J2.pin2, S2.4
  N5: Componente1.A4/SDA, J3.pin1
  N6: Componente1.A5/SCL, J3.pin2
  N7: Componente1.D9_PWM, Mosfet.pin3
  N8: Componente1.D10_PWM/SS, LED1.green_anode
  N9: Componente1.D11_PWM/MOSI, LED1.common_cathode
  N10: Componente1.D12/MISO, J5.pin1
  N11: Componente1.D13/SCK, J5.pin2, S1.2
  N12: Componente1.D2, LCD1.DB7
  N13: Componente1.D3_PWM, LCD1.DB6
  N14: Componente1.D4, LCD1.DB5
  N15: Componente1.D5_PWM, LCD1.DB4
  N16: Componente1.D6_PWM, LCD1.E
  N17: Componente1.D7, LCD1.RS
  N18: Componente1.5V, LED1.red_anode
  N19: LCD1.VDD, F1.1

notes:
  Matriz de teclado 4x4/
  Keyboard matrix 4x4
  +
  R
  G

custom parts:
  RGB LED (com. cathode, rgb): A 5mm tri-color LED with red, green and blue inside.
